# Fritzing sketch simple-way-use-push-button (saved by Fritzing 0.9.3b)
breadboards: 1

parts:
  Part1 = Arduino Uno (Rev3) - ICSP
  S1 = Pushbutton [package="[THT]"]

nets:
  N1: Part1.GND, S1.Pin_4
  N2: Part1.D2, S1.Pin_2

notes:
  Using push button
  with using external pull resistors
  Here we are using Arduino's internal pull up resistor. Refer to code of this section for more explaination.
