# Fritzing sketch joystick-servo (saved by Fritzing 0.9.3b)
breadboards: 1

parts:
  Mod1 = KY-023 Dual Axis Joystick Module [package="Breakout board"]
  J1 = Basic Servo
  J2 = Basic Servo
  R1 = Resistor [tolerance=±5% power=0.25 resistance=220 package=THT]
  LED1 = LED - 3mm [color="Red (633nm)" current=0.030 package="3 mm [THT]"]
  Part2 = Arduino Uno (Rev3) - ICSP

nets:
  GND: Mod1.GND, LED1.cathode, Part2.GND
  +5V: Mod1.+5V, Part2.5V
  N1: Mod1.VRx, Part2.A0
  N2: Mod1.VRy, Part2.A1
  N3: Mod1.SW, Part2.D2
  N4: J1.pulse, Part2.D6_PWM
  N5: J2.pulse, Part2.D5_PWM
  N6: R1.Pin_0, LED1.anode
  N7: R1.Pin_1, Part2.D4

custom parts:
  KY-023 Dual Axis Joystick Module: KY-023 Dual-Axis Joystick Module.
