# Fritzing sketch Controling-DC-motor-tilt-switch (saved by Fritzing 0.9.3b)

parts:
  Part1 = Arduino Uno (Rev3) - ICSP
  M1 = DC Motor
  Part2 = Breadboard Power Supply Board SMD
  IC1 = L293D [package=THT]

nets:
  N1: Part1.D3_PWM, IC1.In_2
  N2: Part1.D4, IC1.In_1
  N3: Part1.D5_PWM, IC1.Enable_1
  N4: M1.pin_1, IC1.Out_1_(_Controlled_by_Enable_1_)
  N5: M1.pin_2, IC1.Out_2_(_Controlled_by_Enable_1_)
  N6: Part2.VCC, IC1.+Vmotor
  N7: Part2.GND, IC1.0V

notes:
  External 5v DC Supply
  Interfacing Arduino with
  - L293D motor driver
  - DC motor
