# Fritzing sketch hr-sr04-nano-interfacing (saved by Fritzing 0.9.3b)

parts:
  HC-SR04_Sensor_1 = HC-SR04 Ultrasonic Distance Sensor
  Part1 = Arduino Nano (Rev3.0)

nets:
  VCC: HC-SR04_Sensor_1.VCC, Part1.5V
  N1: HC-SR04_Sensor_1.TRIG, Part1.D3
  N2: HC-SR04_Sensor_1.ECHO, Part1.D2
  GND: HC-SR04_Sensor_1.GND, Part1.GND

notes:
  HC-SR04 interfacing with Arduino Nano
